// Logisim project CPU.circ as structural Verilog: 7 circuits, main circuit main
module main (
  input  in_1,
  input  [7:0] in_2,
  output Carry,
  output [7:0] Mul_Carry,
  output [7:0] R4,
  output [7:0] R1,
  output Borrow,
  output [7:0] R3,
  output [7:0] R2
);

  wire a, alu_1_add_en, alu_1_borrow, alu_1_carry, alu_1_mul_en, alu_1_sub_en, ALU_En, and_1_out, b, c,
       Clock, d, Hlt, J, L_S, L_S_J, M_En, MAR_Sel, MDR_Sel, not_1_out, not_2_out, PC_Sel, St_Sel, T1, T2,
       T3, T4, Wr_En;
  wire [1:0] RA, RB, Re_Sel;
  wire [2:0] ALU_Sel;
  wire [7:0] Add_PC, alu_1_mul_carry, alu_1_output, ALU_Out, IAR, In_A, In_B, In_PC, IR_q, MAR, MDR,
       multiplexer_1_out, multiplexer_2_out, multiplexer_3_out, PC, ram_1_data, Res_Data;

  Clock clock_1 (.out(Clock));
  Register #(.width(1)) register_1 (.D(alu_1_borrow), .en(alu_1_sub_en), .Q(Borrow), .clk(Clock));  // open: clr
  Multiplexer #(.width(8), .enable("false")) multiplexer_1 (
    .in0(in_2), .in1(Add_PC), .out(multiplexer_1_out), .sel(in_1));
  ALU alu_1 (
    .IPA(In_A), .IPB(In_B), .Carry(alu_1_carry), .\output (alu_1_output), .Enable(ALU_En),
    .Select_ALU(ALU_Sel), .Borrow(alu_1_borrow), .MUL_Carry(alu_1_mul_carry), .Add_En(alu_1_add_en),
    .Sub_En(alu_1_sub_en), .Mul_En(alu_1_mul_en));
  assign In_PC = not_1_out ? multiplexer_1_out : 8'bz;  // Controlled_Buffer controlled_buffer_1
  not not_1 (not_1_out, J);
  Register ALU_Out_Latch (.D(alu_1_output), .Q(ALU_Out), .clk(Clock));  // open: en, clr
  Register #(.width(1)) register_2 (.D(alu_1_carry), .en(alu_1_add_en), .Q(Carry), .clk(Clock));  // open: clr
  Register register_3 (.D(alu_1_mul_carry), .en(alu_1_mul_en), .Q(Mul_Carry), .clk(Clock));  // open: clr
  Register u_PC (.D(In_PC), .Q(PC), .clk(Clock));  // open: en, clr
  RAM ram_1 (.addr(IAR), .data(ram_1_data), .sel(M_En), .clk(Clock), .ld(not_2_out));  // open: clr
  not not_2 (not_2_out, St_Sel);
  assign ram_1_data = St_Sel ? In_A : 8'bz;  // Controlled_Buffer controlled_buffer_2
  Multiplexer #(.width(8), .enable("false")) multiplexer_2 (
    .in0({8{1'b0}}), .in1(ram_1_data), .out(multiplexer_2_out), .sel(in_1));
  Multiplexer #(.width(8), .enable("false")) multiplexer_3 (
    .in0({8{1'b0}}), .in1(8'h1), .out(multiplexer_3_out), .sel(PC_Sel));
  Register_File register_file_1 (
    .Clock(Clock), .Address_A(RA), .Address_B(RB), .Write_Data(Res_Data), .In_A(In_A), .In_B(In_B), .R1(R1),
    .R2(R2), .R3(R3), .R4(R4), .Address_C(RA), .Enable(Wr_En));
  Adder adder_1 (.a(PC), .b(multiplexer_3_out), .out(Add_PC));  // open: cin, cout
  Register u_MAR (.D(multiplexer_2_out), .en(MAR_Sel), .Q(MAR), .clk(Clock));  // open: clr
  Register IR (.D(multiplexer_2_out), .en(T1), .Q(IR_q), .clk(Clock));  // open: clr
  Register u_MDR (.D(multiplexer_2_out), .en(MDR_Sel), .Q(MDR), .clk(Clock));  // open: clr
  Decode decode_1 (.INS(IR_q), .a(a), .b(b), .c(c), .d(d), .RA(RA), .RB(RB));
  Multiplexer #(.width(8), .enable("false")) multiplexer_4 (.in0(Add_PC), .in1(MAR), .out(IAR), .sel(and_1_out));
  and and_1 (and_1_out, L_S_J, T3);
  assign In_PC = J ? IAR : 8'bz;  // Controlled_Buffer controlled_buffer_3
  Signals signals_1 (
    .a(a), .b(b), .c(c), .d(d), .S(in_1), .T1(T1), .T2(T2), .T3(T3), .T4(T4), .L_S(L_S), .J(J),
    .L_S_J(L_S_J), .Memory_Enable(M_En), .Hlt(Hlt), .ALU_Sel(ALU_Sel), .PC_Sel(PC_Sel), .ALU_En(ALU_En),
    .MAR_Sel(MAR_Sel), .MDR_Sel(MDR_Sel), .St_Sel(St_Sel), .Wr_En(Wr_En), .Re_Sel(Re_Sel));
  Step_Counter step_counter_1 (.Clock(Clock), .Couner_Enable(in_1), .T1(T1), .T2(T2), .T3(T3), .T4(T4));
  Multiplexer #(.select(2), .width(8), .enable("false")) multiplexer_5 (
    .in0(ALU_Out), .in1(MDR), .in2(In_B), .out(Res_Data), .sel(Re_Sel));  // open: in3

  // Other names for the same wires on the sheet: S = in_1

  // Notes on the sheet:
  //   Switch
  //   ALU
  //                                                    Memory
  //   Instruction Address Generator
  //   Register File
  //   Control Signals
  //   MUX Y
  //   StepCounter
endmodule

module ADD (
  input  C0,
  input  [7:0] IPA,
  input  [7:0] IPB,
  output F_Carry,
  output [7:0] OP
);

  wire adder_2_cout, adder_3_cout, adder_4_cout, adder_5_cout, adder_6_cout, adder_7_cout, adder_8_cout;

  Adder #(.width(1)) adder_1 (.a(IPA[7]), .b(IPB[7]), .out(OP[7]), .cin(adder_2_cout), .cout(F_Carry));
  Adder #(.width(1)) adder_2 (.a(IPA[6]), .b(IPB[6]), .out(OP[6]), .cin(adder_3_cout), .cout(adder_2_cout));
  Adder #(.width(1)) adder_3 (.a(IPA[5]), .b(IPB[5]), .out(OP[5]), .cin(adder_4_cout), .cout(adder_3_cout));
  Adder #(.width(1)) adder_4 (.a(IPA[4]), .b(IPB[4]), .out(OP[4]), .cin(adder_5_cout), .cout(adder_4_cout));
  Adder #(.width(1)) adder_5 (.a(IPA[3]), .b(IPB[3]), .out(OP[3]), .cin(adder_6_cout), .cout(adder_5_cout));
  Adder #(.width(1)) adder_6 (.a(IPA[2]), .b(IPB[2]), .out(OP[2]), .cin(adder_7_cout), .cout(adder_6_cout));
  Adder #(.width(1)) adder_7 (.a(IPA[1]), .b(IPB[1]), .out(OP[1]), .cin(adder_8_cout), .cout(adder_7_cout));
  Adder #(.width(1)) adder_8 (.a(IPA[0]), .b(IPB[0]), .out(OP[0]), .cin(C0), .cout(adder_8_cout));

  // Other names for the same wires on the sheet: A0 = IPA[0]; A1 = IPA[1]; A2 = IPA[2]; A3 = IPA[3]; A4 = IPA[4];
  //   A5 = IPA[5]; A6 = IPA[6]; A7 = IPA[7]; B0 = IPB[0]; B1 = IPB[1]; B2 = IPB[2]; B3 = IPB[3]; B4 = IPB[4];
  //   B5 = IPB[5]; B6 = IPB[6]; B7 = IPB[7]
endmodule

module ALU (
  input  Enable,
  input  [2:0] Select_ALU,
  input  [7:0] IPA,
  input  [7:0] IPB,
  output Carry,
  output [7:0] \output ,
  output Add_En,
  output Sub_En,
  output Borrow,
  output [7:0] MUL_Carry,
  output Mul_En
);

  wire not_2_out, not_3_out, not_4_out, not_5_out, not_6_out, not_7_out, not_8_out;
  wire [7:0] not_1_out, op0, op1, op2, op3, op4, op5, Tmp1;

  Multiplier multiplier_1 (.a(IPA), .b(IPB), .out(op2), .cout(MUL_Carry));  // open: cin
  assign op4 = IPA | IPB;  // OR_Gate or_1, 8 bits wide
  assign op3 = IPA & IPB;  // AND_Gate and_1, 8 bits wide
  assign op5 = IPA ^ IPB;  // XOR_Gate xor_1, 8 bits wide
  assign not_1_out = ~IPB;  // NOT_Gate not_1, 8 bits wide
  ADD add_1 (.C0(1'b0), .IPA(IPA), .IPB(IPB), .F_Carry(Carry), .OP(op0));
  ADD add_2 (.C0(1'b0), .IPA(not_1_out), .IPB(8'h1), .OP(Tmp1));  // open: F_Carry
  ADD add_3 (.C0(1'b0), .IPA(IPA), .IPB(Tmp1), .F_Carry(Borrow), .OP(op1));
  Multiplexer #(.select(3), .width(8)) multiplexer_1 (
    .in0(op0), .in1(op1), .in2(op2), .in3(op3), .in4(op4), .in5(op5), .out(\output ), .sel(Select_ALU),
    .en(Enable));  // open: in6, in7
  not not_2 (not_2_out, Select_ALU[1]);
  not not_3 (not_3_out, Select_ALU[2]);
  and and_2 (Add_En, not_3_out, not_2_out, not_5_out, Enable);
  not not_4 (not_4_out, Select_ALU[2]);
  and and_3 (Mul_En, not_4_out, Select_ALU[1], not_6_out, Enable);
  not not_5 (not_5_out, Select_ALU[0]);
  not not_6 (not_6_out, Select_ALU[0]);
  not not_7 (not_7_out, Select_ALU[1]);
  not not_8 (not_8_out, Select_ALU[2]);
  and and_4 (Sub_En, not_8_out, not_7_out, Select_ALU[0], Enable);

  // Other names for the same wires on the sheet: En = Enable; A0 = IPA[0]; InputA[7:0] = IPA; A1 = IPA[1];
  //   A2 = IPA[2]; A3 = IPA[3]; A4 = IPA[4]; A5 = IPA[5]; A6 = IPA[6]; A7 = IPA[7]; B0 = IPB[0]; InputB[7:0] = IPB;
  //   B1 = IPB[1]; B2 = IPB[2]; B3 = IPB[3]; B4 = IPB[4]; B5 = IPB[5]; B6 = IPB[6]; B7 = IPB[7]; c = Select_ALU[0];
  //   Select[2:0] = Select_ALU; b = Select_ALU[1]; a = Select_ALU[2]
endmodule

// Reg File
module Register_File (
  input  Clock,
  input  Enable,
  input  [7:0] Write_Data,
  input  [1:0] Address_A,
  input  [1:0] Address_B,
  input  [1:0] Address_C,
  output [7:0] In_A,
  output [7:0] In_B,
  output [7:0] R1,
  output [7:0] R2,
  output [7:0] R3,
  output [7:0] R4
);

  wire En1, En2, En3, En4;
  wire [7:0] In1, In2, In3, In4;

  Multiplexer #(.select(2), .width(8), .enable("false")) multiplexer_1 (
    .in0(R1), .in1(R2), .in2(R3), .in3(R4), .out(In_A), .sel(Address_A));
  Register register_1 (.D(In1), .en(En1), .Q(R1), .clk(Clock));  // open: clr
  Multiplexer #(.select(2), .width(8), .enable("false")) multiplexer_2 (
    .in0(R1), .in1(R2), .in2(R3), .in3(R4), .out(In_B), .sel(Address_B));
  Register register_2 (.D(In2), .en(En2), .Q(R2), .clk(Clock));  // open: clr
  Register register_3 (.D(In3), .en(En3), .Q(R3), .clk(Clock));  // open: clr
  Demultiplexer #(.select(2), .enable("false")) demultiplexer_1 (
    .out0(En1), .out1(En2), .out2(En3), .out3(En4), .in(Enable), .sel(Address_C));
  Register register_4 (.D(In4), .en(En4), .Q(R4), .clk(Clock));  // open: clr
  Demultiplexer #(.select(2), .width(8), .enable("false")) demultiplexer_2 (
    .out0(In1), .out1(In2), .out2(In3), .out3(In4), .in(Write_Data), .sel(Address_C));

  // Other names for the same wires on the sheet: Out1[7:0] = R1; Out2[7:0] = R2; Out3[7:0] = R3; Out4[7:0] = R4
endmodule

module Step_Counter (
  input  Couner_Enable,
  input  Clock,
  output T1,
  output T2,
  output T3,
  output T4
);

  wire not_1_out;
  wire [1:0] counter_1_q;

  Counter #(.width(2), .max('h3)) counter_1 (
    .D(2'b11), .Q(counter_1_q), .clk(Clock), .clr(not_1_out));  // open: load, count, carry
  not not_1 (not_1_out, Couner_Enable);
  Decoder #(.select(2)) decoder_1 (.out0(T1), .out1(T2), .out2(T3), .out3(T4), .sel(counter_1_q), .en(Couner_Enable));
endmodule

module Decode (
  input  [7:0] INS,
  output a,
  output b,
  output c,
  output d,
  output [1:0] RA,
  output [1:0] RB
);


  assign a = INS[7];
  assign b = INS[6];
  assign c = INS[5];
  assign d = INS[4];
  assign RA = INS[3:2];
  assign RB = INS[1:0];
endmodule

// Ctrl Signals
module Signals (
  input  a,
  input  b,
  input  c,
  input  d,
  input  S,
  input  T1,
  input  T2,
  input  T3,
  input  T4,
  output MAR_Sel,
  output MDR_Sel,
  output L_S,
  output J,
  output L_S_J,
  output Memory_Enable,
  output [2:0] ALU_Sel,
  output ALU_En,
  output St_Sel,
  output Hlt,
  output Wr_En,
  output PC_Sel,
  output [1:0] Re_Sel
);

  wire and_5_out, and_6_out, and_8_out, and_9_out, and_10_out, and_13_out, not_1_out, not_2_out, not_3_out,
       not_4_out, not_5_out, not_6_out, not_7_out, not_8_out, not_9_out, not_10_out, not_11_out, not_12_out,
       not_13_out, not_14_out, not_15_out, not_16_out, or_3_out;

  not not_1 (not_1_out, b);
  and and_1 (L_S, a, not_1_out, not_4_out);
  not not_2 (not_2_out, a);
  and and_2 (Hlt, not_2_out, b, c, d);
  not not_3 (not_3_out, a);
  and and_3 (Re_Sel[1], not_3_out, b, c, not_5_out);
  not not_4 (not_4_out, c);
  not not_5 (not_5_out, d);
  not not_6 (not_6_out, b);
  and and_4 (J, a, not_6_out, c, not_7_out);
  not not_7 (not_7_out, d);
  not not_8 (not_8_out, L_S_J);
  not not_9 (not_9_out, Hlt);
  not not_10 (not_10_out, b);
  not not_11 (not_11_out, d);
  and and_5 (and_5_out, a, not_10_out, not_11_out);
  or or_1 (L_S_J, and_5_out, L_S);
  and and_6 (and_6_out, T2, not_8_out);
  and and_7 (ALU_En, and_6_out, not_9_out);
  and and_8 (and_8_out, S, T1);
  and and_9 (and_9_out, S, a);
  or or_2 (Memory_Enable, and_8_out, and_9_out);
  not not_12 (not_12_out, Hlt);
  and and_10 (and_10_out, a, T3);
  or or_3 (or_3_out, and_10_out, T2);
  and and_11 (PC_Sel, or_3_out, not_12_out);
  and and_12 (MAR_Sel, T2, a);
  not not_13 (not_13_out, J);
  and and_13 (and_13_out, L_S, d);
  not not_14 (not_14_out, and_13_out);
  and and_14 (Wr_En, T4, not_14_out, not_13_out, not_15_out);
  not not_15 (not_15_out, Hlt);
  not not_16 (not_16_out, d);
  and and_15 (MDR_Sel, T3, L_S, not_16_out);
  and and_16 (St_Sel, T3, L_S, d);

  assign ALU_Sel = {b, c, d};
  assign Re_Sel[0] = a;

  // Other names for the same wires on the sheet: Mv = Re_Sel[1]
endmodule
